// Logisim project dinoGame.circ as structural Verilog
module main (
  input  \_0_1_속도_조절_필요____how ,
  input  [7:0] in_2,
  input  [7:0] in_3,
  input  in_4,
  input  [7:0] in_5,
  input  in_6,
  input  in_7,
  input  [7:0] in_8,
  input  [7:0] in_9,
  input  [7:0] in_10,
  input  [7:0] in_11,
  input  [7:0] in_12,
  input  [7:0] in_13,
  input  [7:0] in_14,
  input  [7:0] in_15
);

  wire clock_1_out, clock_2_out;
  wire [7:0] ground_1_out_5, ground_1_out_6, ground_1_out_7, ground_1_out_8, ground_1_out_9, ground_1_out_10,
       ground_1_out_11, ground_1_out_12, jump_1_out_7, or_1_out;

  Clock clock_1 (.out(clock_1_out));
  DotMatrix #(.matrixcols(8), .matrixrows(8)) dotmatrix_1 (
    .col0(ground_1_out_7), .col1(ground_1_out_8), .col2(ground_1_out_9), .col3(ground_1_out_10),
    .col4(ground_1_out_5), .col5(ground_1_out_11), .col6(or_1_out), .col7(ground_1_out_12));
  Ground ground_1 (
    .\input (in_5), .start(in_6), .clock(clock_1_out), .reset(in_7), .out_7(ground_1_out_7),
    .out_8(ground_1_out_8), .out_9(ground_1_out_9), .out_10(ground_1_out_10), .out_5(ground_1_out_5),
    .out_11(ground_1_out_11), .out_6(ground_1_out_6), .out_12(ground_1_out_12));
  assign or_1_out = jump_1_out_7 | ground_1_out_6;  // OR_Gate or_1, 8 bits wide
  Clock #(.highDuration(10), .lowDuration(10)) clock_2 (.out(clock_2_out));
  jump jump_1 (
    .in_1(in_2), .in_2(in_3), .jump(\_0_1_속도_조절_필요____how ), .enable(in_4), .clock(clock_2_out),
    .out_7(jump_1_out_7));  // open: reset
  DotMatrix #(.matrixcols(8), .matrixrows(8)) dotmatrix_2 (
    .col0(in_8), .col1(in_8), .col2(in_9), .col3(in_13), .col4(in_10), .col5(in_14), .col6(in_11),
    .col7(in_15));

  assign in_12 = in_8;
endmodule

module Ground (
  input  [7:0] \input ,
  input  start,
  input  clock,
  input  reset,
  output [7:0] out_5,
  output [7:0] out_6,
  output [7:0] out_7,
  output [7:0] out_8,
  output [7:0] out_9,
  output [7:0] out_10,
  output [7:0] out_11,
  output [7:0] out_12
);

  Register register_1 (.D(\input ), .en(start), .Q(out_7), .clk(clock), .clr(reset));
  Register register_2 (.D(out_7), .en(start), .Q(out_8), .clk(clock), .clr(reset));
  Register register_3 (.D(out_8), .en(start), .Q(out_9), .clk(clock), .clr(reset));
  Register register_4 (.D(out_9), .Q(out_10), .clk(clock), .clr(reset));  // open: en
  Register register_5 (.D(out_10), .en(start), .Q(out_5), .clk(clock), .clr(reset));
  Register register_6 (.D(out_5), .en(start), .Q(out_11), .clk(clock), .clr(reset));
  Register register_7 (.D(out_11), .en(start), .Q(out_6), .clk(clock), .clr(reset));
  Register register_8 (.D(out_6), .en(start), .Q(out_12), .clk(clock), .clr(reset));
endmodule

module jump (
  input  [7:0] in_1,
  input  [7:0] in_2,
  input  jump,
  input  enable,
  input  clock,
  input  reset,
  output [7:0] out_7
);

  wire undriven;
  wire [7:0] multiplexer_1_out;

  Multiplexer #(.width(8)) multiplexer_1 (.in0(in_1), .in1(in_2), .out(multiplexer_1_out), .sel(jump));  // open: en
  Register register_1 (.D(multiplexer_1_out), .en(undriven), .Q(out_7), .clk(clock), .clr(reset));
endmodule

module pushBump (
  input  [31:0] empty_block,
  input  [31:0] block5,
  input  [31:0] block4,
  input  [31:0] block3,
  input  [31:0] block2,
  input  [31:0] block1,
  input  start,
  input  clock,
  input  reset,
  input  making,
  output [31:0] \output 
);

  wire not_1_out;
  wire [31:0] controlled_buffer_1_out, controlled_buffer_3_out, controlled_buffer_5_out,
       controlled_buffer_7_out, controlled_buffer_9_out, register_1_q, register_2_q, register_3_q,
       register_4_q, register_5_q, register_6_q;

  not not_1 (not_1_out, making);
  assign controlled_buffer_1_out = making ? block5 : 32'bz;  // Controlled_Buffer controlled_buffer_1
  Register #(.width(32)) register_1 (.D(empty_block), .en(start), .Q(register_1_q), .clk(clock), .clr(reset));
  assign controlled_buffer_1_out = not_1_out ? register_1_q : 32'bz;  // Controlled_Buffer controlled_buffer_2
  assign controlled_buffer_3_out = making ? block4 : 32'bz;  // Controlled_Buffer controlled_buffer_3
  assign controlled_buffer_3_out = not_1_out ? register_2_q : 32'bz;  // Controlled_Buffer controlled_buffer_4
  Register #(.width(32)) register_2 (
    .D(controlled_buffer_1_out), .en(start), .Q(register_2_q), .clk(clock), .clr(reset));
  Register #(.width(32)) register_3 (
    .D(controlled_buffer_3_out), .en(start), .Q(register_3_q), .clk(clock), .clr(reset));
  assign controlled_buffer_5_out = making ? block3 : 32'bz;  // Controlled_Buffer controlled_buffer_5
  assign controlled_buffer_5_out = not_1_out ? register_3_q : 32'bz;  // Controlled_Buffer controlled_buffer_6
  assign controlled_buffer_7_out = not_1_out ? register_4_q : 32'bz;  // Controlled_Buffer controlled_buffer_7
  Register #(.width(32)) register_4 (
    .D(controlled_buffer_5_out), .en(start), .Q(register_4_q), .clk(clock), .clr(reset));
  assign controlled_buffer_7_out = making ? block2 : 32'bz;  // Controlled_Buffer controlled_buffer_8
  Register #(.width(32)) register_5 (
    .D(controlled_buffer_7_out), .en(start), .Q(register_5_q), .clk(clock), .clr(reset));
  assign controlled_buffer_9_out = not_1_out ? register_5_q : 32'bz;  // Controlled_Buffer controlled_buffer_9
  assign controlled_buffer_9_out = making ? block1 : 32'bz;  // Controlled_Buffer controlled_buffer_10
  Register #(.width(32)) register_6 (
    .D(controlled_buffer_9_out), .en(start), .Q(register_6_q), .clk(clock), .clr(reset));
  Register #(.width(32)) register_7 (.D(register_6_q), .en(start), .Q(\output ), .clk(clock), .clr(reset));
endmodule

module pushBumpTest (
  input  [7:0] empty_block,
  input  [7:0] block2,
  input  [7:0] block1,
  input  start,
  input  clock,
  input  reset,
  input  making,
  output [7:0] \output 
);

  wire not_1_out;
  wire [7:0] controlled_buffer_1_out, controlled_buffer_2_out, controlled_buffer_4_out, register_1_q,
       register_2_q, register_3_q, register_4_q;

  not not_1 (not_1_out, making);
  Register register_1 (.D(empty_block), .en(start), .Q(register_1_q), .clk(clock), .clr(reset));
  assign controlled_buffer_1_out = not_1_out ? register_1_q : 8'bz;  // Controlled_Buffer controlled_buffer_1
  assign controlled_buffer_2_out = not_1_out ? register_2_q : 8'bz;  // Controlled_Buffer controlled_buffer_2
  Register register_2 (.D(controlled_buffer_1_out), .en(start), .Q(register_2_q), .clk(clock), .clr(reset));
  assign controlled_buffer_2_out = making ? block2 : 8'bz;  // Controlled_Buffer controlled_buffer_3
  assign controlled_buffer_4_out = not_1_out ? register_3_q : 8'bz;  // Controlled_Buffer controlled_buffer_4
  Register register_3 (.D(controlled_buffer_2_out), .en(start), .Q(register_3_q), .clk(clock), .clr(reset));
  assign controlled_buffer_4_out = making ? block1 : 8'bz;  // Controlled_Buffer controlled_buffer_5
  Register register_4 (.D(controlled_buffer_4_out), .en(start), .Q(register_4_q), .clk(clock), .clr(reset));
  Register register_5 (.D(register_4_q), .en(start), .Q(\output ), .clk(clock), .clr(reset));
endmodule
