// Logisim project jump.circ as structural Verilog: 1 circuit, main circuit main
module main (
  input  [7:0] in_1,
  input  [7:0] in_2,
  input  jump,
  input  enable,
  input  clock,
  input  reset,
  output [7:0] out_7
);

  wire undriven;
  wire [7:0] multiplexer_1_out;

  Multiplexer #(.width(8)) multiplexer_1 (.in0(in_1), .in1(in_2), .out(multiplexer_1_out), .sel(jump));  // open: en
  Register register_1 (.D(multiplexer_1_out), .en(undriven), .Q(out_7), .clk(clock), .clr(reset));
endmodule
