// Logisim project jump32.circ as structural Verilog: 1 circuit, main circuit jump32
module jump32 (
  input  isJump,
  input  clock,
  input  [31:0] character1,
  input  [31:0] character2,
  input  [31:0] character3,
  input  [31:0] character4,
  output [31:0] out_7,
  output [31:0] out_8,
  output [31:0] out_9,
  output [31:0] out_10
);

  wire and_1_out, counter_1_carry, not_1_out, not_2_out;
  wire [2:0] counter_1_q;
  wire [4:0] multiplexer_1_out;

  not not_1 (not_1_out, counter_1_carry);
  not not_2 (not_2_out, isJump);
  and and_1 (and_1_out, clock, not_1_out);
  Counter #(.width(3), .max('h4)) counter_1 (
    .load(not_2_out), .Q(counter_1_q), .carry(counter_1_carry), .clk(and_1_out));  // open: D, count, clr
  Multiplexer #(.select(3), .width(5)) multiplexer_1 (
    .in0({5{1'b0}}), .in1(5'b01000), .in2(5'b01100), .in3(5'b01110), .in4(5'b01110), .out(multiplexer_1_out),
    .sel(counter_1_q), .en(1'b1));  // open: in5, in6, in7
  Shifter #(.width(32)) shifter_1 (.in(character1), .\dist (multiplexer_1_out), .out(out_7));
  Shifter #(.width(32)) shifter_2 (.in(character2), .\dist (multiplexer_1_out), .out(out_8));
  Shifter #(.width(32)) shifter_3 (.in(character3), .\dist (multiplexer_1_out), .out(out_9));
  Shifter #(.width(32)) shifter_4 (.in(character4), .\dist (multiplexer_1_out), .out(out_10));

  // Notes on the sheet:
  //   animation frame
  //   character
  //   distance
  //   output_character
endmodule
