// Logisim project pushBump32.circ as structural Verilog: 1 circuit, main circuit pushBump32
module pushBump32 (
  input  [31:0] empty_block,
  input  [31:0] block5,
  input  [31:0] block4,
  input  [31:0] block3,
  input  [31:0] block2,
  input  [31:0] block1,
  input  start,
  input  clock,
  input  reset,
  input  making,
  output [31:0] \output 
);

  wire not_1_out;
  wire [31:0] controlled_buffer_1_out, controlled_buffer_3_out, controlled_buffer_5_out,
       controlled_buffer_7_out, controlled_buffer_9_out, register_1_q, register_2_q, register_3_q,
       register_4_q, register_5_q, register_6_q;

  not not_1 (not_1_out, making);
  assign controlled_buffer_1_out = making ? block5 : 32'bz;  // Controlled_Buffer controlled_buffer_1
  Register #(.width(32)) register_1 (.D(empty_block), .en(start), .Q(register_1_q), .clk(clock), .clr(reset));
  assign controlled_buffer_1_out = not_1_out ? register_1_q : 32'bz;  // Controlled_Buffer controlled_buffer_2
  assign controlled_buffer_3_out = making ? block4 : 32'bz;  // Controlled_Buffer controlled_buffer_3
  Register #(.width(32)) register_2 (
    .D(controlled_buffer_1_out), .en(start), .Q(register_2_q), .clk(clock), .clr(reset));
  assign controlled_buffer_3_out = not_1_out ? register_2_q : 32'bz;  // Controlled_Buffer controlled_buffer_4
  Register #(.width(32)) register_3 (
    .D(controlled_buffer_3_out), .en(start), .Q(register_3_q), .clk(clock), .clr(reset));
  assign controlled_buffer_5_out = making ? block3 : 32'bz;  // Controlled_Buffer controlled_buffer_5
  assign controlled_buffer_5_out = not_1_out ? register_3_q : 32'bz;  // Controlled_Buffer controlled_buffer_6
  assign controlled_buffer_7_out = not_1_out ? register_4_q : 32'bz;  // Controlled_Buffer controlled_buffer_7
  Register #(.width(32)) register_4 (
    .D(controlled_buffer_5_out), .en(start), .Q(register_4_q), .clk(clock), .clr(reset));
  assign controlled_buffer_7_out = making ? block2 : 32'bz;  // Controlled_Buffer controlled_buffer_8
  assign controlled_buffer_9_out = not_1_out ? register_5_q : 32'bz;  // Controlled_Buffer controlled_buffer_9
  Register #(.width(32)) register_5 (
    .D(controlled_buffer_7_out), .en(start), .Q(register_5_q), .clk(clock), .clr(reset));
  assign controlled_buffer_9_out = making ? block1 : 32'bz;  // Controlled_Buffer controlled_buffer_10
  Register #(.width(32)) register_6 (
    .D(controlled_buffer_9_out), .en(start), .Q(register_6_q), .clk(clock), .clr(reset));
  Register #(.width(32)) register_7 (.D(register_6_q), .en(start), .Q(\output ), .clk(clock), .clr(reset));
endmodule
