// Logisim project test.circ as structural Verilog: 1 circuit, main circuit main
module main (
  input  start,
  input  reset,
  input  [7:0] delayTime,
  output isBumped
);

  wire bumpCounter_output, bumpIncoder_clock_output, bumpIncoder_reset_output, bumpIncoder_start_output,
       clock_2_out, clock_out, controlled_buffer_1_out, jump_out, nor_1_out, nor_2_out, not_1_out;
  wire [31:0] bumpIncoder_2_display1, bumpIncoder_2_display2, bumpIncoder_2_display3, bumpIncoder_2_display4,
       bumpIncoder_2_display5, bumpIncoder_2_display6, bumpIncoder_2_display7, bumpIncoder_2_display8,
       bumpIncoder_2_display9, bumpIncoder_2_display10, bumpIncoder_2_display11, bumpIncoder_2_display12,
       bumpIncoder_2_display13, bumpIncoder_2_display14, bumpIncoder_2_display15, bumpIncoder_2_display16,
       bumpIncoder_2_display17, bumpIncoder_2_display18, bumpIncoder_2_display19, bumpIncoder_2_display20,
       bumpIncoder_2_display21, bumpIncoder_2_display22, bumpIncoder_2_display23, bumpIncoder_2_display24,
       bumpIncoder_2_display25, bumpIncoder_2_display26, bumpIncoder_2_display27, bumpIncoder_2_display28,
       bumpIncoder_2_display29, bumpIncoder_2_display30, bumpIncoder_2_display31, bumpIncoder_2_display32,
       bumpIncoder_display1, bumpIncoder_display2, bumpIncoder_display3, bumpIncoder_display4,
       bumpIncoder_display5, bumpIncoder_display6, bumpIncoder_display7, bumpIncoder_display8,
       bumpIncoder_display9, bumpIncoder_display10, bumpIncoder_display11, bumpIncoder_display12,
       bumpIncoder_display13, bumpIncoder_display14, bumpIncoder_display15, bumpIncoder_display16,
       bumpIncoder_display17, bumpIncoder_display18, bumpIncoder_display19, bumpIncoder_display20,
       bumpIncoder_display21, bumpIncoder_display22, bumpIncoder_display23, bumpIncoder_display24,
       bumpIncoder_display25, bumpIncoder_display26, bumpIncoder_display27, bumpIncoder_display28,
       bumpIncoder_display29, bumpIncoder_display30, bumpIncoder_display31, bumpIncoder_display32,
       bumpIncoder_final_data, jump32_1_out_7, jump32_1_out_8, jump32_1_out_9, jump32_1_out_10,
       pushBump_output;

  Clock clock (.out(clock_out));
  assign controlled_buffer_1_out = not_1_out ? clock_out : 1'bz;  // Controlled_Buffer controlled_buffer_1
  not not_1 (not_1_out, nor_1_out);
  pushBump32 pushBump (
    .start(start), .clock(controlled_buffer_1_out), .reset(reset), .making(bumpCounter_output),
    .ground(32'h1), .block1(32'h28), .block2(32'h1e), .block3(32'h30), .block4({32{1'b0}}),
    .\output (pushBump_output));
  bumpCounter bumpCounter (
    .delayTime(8'h20), .start(start), .clock(controlled_buffer_1_out), .\output (bumpCounter_output));
  DotMatrix #(.matrixcols(32), .matrixrows(32)) dotmatrix_1 (
    .col0(bumpIncoder_display1), .col1(bumpIncoder_display2), .col2(bumpIncoder_display3),
    .col3(bumpIncoder_display4), .col4(bumpIncoder_display5), .col5(bumpIncoder_display6),
    .col6(bumpIncoder_display7), .col7(bumpIncoder_display8), .col8(bumpIncoder_display9),
    .col9(bumpIncoder_display10), .col10(bumpIncoder_display11), .col11(bumpIncoder_display12),
    .col12(bumpIncoder_display13), .col13(bumpIncoder_display14), .col14(bumpIncoder_display15),
    .col15(bumpIncoder_display16), .col16(bumpIncoder_display17), .col17(bumpIncoder_display18),
    .col18(bumpIncoder_display19), .col19(bumpIncoder_display20), .col20(bumpIncoder_display21),
    .col21(bumpIncoder_display22), .col22(bumpIncoder_display23), .col23(bumpIncoder_display24),
    .col24(bumpIncoder_display25), .col25(bumpIncoder_display26), .col26(bumpIncoder_display27),
    .col27(bumpIncoder_display28), .col28(bumpIncoder_display29), .col29(bumpIncoder_display30),
    .col30(bumpIncoder_display31), .col31(bumpIncoder_display32));
  nor nor_1 (nor_1_out, nor_2_out, reset);
  nor nor_2 (nor_2_out, nor_1_out, isBumped);
  DotMatrix #(.matrixcols(32), .matrixrows(32)) dotmatrix_2 (
    .col0(bumpIncoder_2_display1), .col1(bumpIncoder_2_display2), .col2(bumpIncoder_2_display3),
    .col3(bumpIncoder_2_display4), .col4(bumpIncoder_2_display5), .col5(bumpIncoder_2_display6),
    .col6(bumpIncoder_2_display7), .col7(bumpIncoder_2_display8), .col8(bumpIncoder_2_display9),
    .col9(bumpIncoder_2_display10), .col10(bumpIncoder_2_display11), .col11(bumpIncoder_2_display12),
    .col12(bumpIncoder_2_display13), .col13(bumpIncoder_2_display14), .col14(bumpIncoder_2_display15),
    .col15(bumpIncoder_2_display16), .col16(bumpIncoder_2_display17), .col17(bumpIncoder_2_display18),
    .col18(bumpIncoder_2_display19), .col19(bumpIncoder_2_display20), .col20(bumpIncoder_2_display21),
    .col21(bumpIncoder_2_display22), .col22(bumpIncoder_2_display23), .col23(bumpIncoder_2_display24),
    .col24(bumpIncoder_2_display25), .col25(bumpIncoder_2_display26), .col26(bumpIncoder_2_display27),
    .col27(bumpIncoder_2_display28), .col28(bumpIncoder_2_display29), .col29(bumpIncoder_2_display30),
    .col30(bumpIncoder_2_display31), .col31(bumpIncoder_2_display32));
  bumpIncoder32 bumpIncoder (
    .start_data(pushBump_output), .start(start), .clock(controlled_buffer_1_out), .reset(reset),
    .display1(bumpIncoder_display1), .display2(bumpIncoder_display2), .display3(bumpIncoder_display3),
    .display4(bumpIncoder_display4), .display5(bumpIncoder_display5), .display6(bumpIncoder_display6),
    .display7(bumpIncoder_display7), .display8(bumpIncoder_display8), .display9(bumpIncoder_display9),
    .display10(bumpIncoder_display10), .display11(bumpIncoder_display11), .display12(bumpIncoder_display12),
    .display13(bumpIncoder_display13), .display14(bumpIncoder_display14), .display15(bumpIncoder_display15),
    .display16(bumpIncoder_display16), .display17(bumpIncoder_display17), .display18(bumpIncoder_display18),
    .display19(bumpIncoder_display19), .display20(bumpIncoder_display20), .display21(bumpIncoder_display21),
    .display22(bumpIncoder_display22), .display23(bumpIncoder_display23), .display24(bumpIncoder_display24),
    .display25(bumpIncoder_display25), .display26(bumpIncoder_display26), .display27(bumpIncoder_display27),
    .display28(bumpIncoder_display28), .display29(bumpIncoder_display29), .display30(bumpIncoder_display30),
    .display31(bumpIncoder_display31), .display32(bumpIncoder_display32), .character1({32{1'b0}}),
    .character2({32{1'b0}}), .character3({32{1'b0}}), .character4({32{1'b0}}),
    .final_data(bumpIncoder_final_data), .start_output(bumpIncoder_start_output),
    .clock_output(bumpIncoder_clock_output), .reset_output(bumpIncoder_reset_output));  // open: isBumped
  Button jump (.out(jump_out));
  jump32 jump32_1 (
    .character1(32'h6e), .character2(32'h3c), .character3(32'h2c), .character4(32'h7e), .isJump(jump_out),
    .clock(clock_2_out), .out_7(jump32_1_out_7), .out_8(jump32_1_out_8), .out_9(jump32_1_out_9),
    .out_10(jump32_1_out_10));
  Clock #(.lowDuration(4)) clock_2 (.out(clock_2_out));
  bumpIncoder32 bumpIncoder_2 (
    .start_data(bumpIncoder_final_data), .start(bumpIncoder_start_output), .clock(bumpIncoder_clock_output),
    .reset(bumpIncoder_reset_output), .display1(bumpIncoder_2_display1), .display2(bumpIncoder_2_display2),
    .display3(bumpIncoder_2_display3), .display4(bumpIncoder_2_display4), .display5(bumpIncoder_2_display5),
    .display6(bumpIncoder_2_display6), .display7(bumpIncoder_2_display7), .display8(bumpIncoder_2_display8),
    .display9(bumpIncoder_2_display9), .display10(bumpIncoder_2_display10),
    .display11(bumpIncoder_2_display11), .display12(bumpIncoder_2_display12),
    .display13(bumpIncoder_2_display13), .display14(bumpIncoder_2_display14),
    .display15(bumpIncoder_2_display15), .display16(bumpIncoder_2_display16),
    .display17(bumpIncoder_2_display17), .display18(bumpIncoder_2_display18),
    .display19(bumpIncoder_2_display19), .display20(bumpIncoder_2_display20),
    .display21(bumpIncoder_2_display21), .display22(bumpIncoder_2_display22),
    .display23(bumpIncoder_2_display23), .display24(bumpIncoder_2_display24),
    .display25(bumpIncoder_2_display25), .display26(bumpIncoder_2_display26),
    .display27(bumpIncoder_2_display27), .display28(bumpIncoder_2_display28),
    .display29(bumpIncoder_2_display29), .display30(bumpIncoder_2_display30),
    .display31(bumpIncoder_2_display31), .display32(bumpIncoder_2_display32), .character1(jump32_1_out_7),
    .character2(jump32_1_out_8), .character3(jump32_1_out_9), .character4(jump32_1_out_10),
    .isBumped(isBumped));  // open: final_data, start_output, clock_output, reset_output

  // Notes on the sheet:
  //   2. clock 활성화
  //   3. start버튼 누른 후 시작
  //   1. 리셋 버튼 눌러서 빨간전선 없애기
  //   점수 스크린 만들 곳
endmodule
